// Digital circuit multiplicador2bits.dig as structural Verilog
module multiplicador2bits (
  input  B0,
  input  A0,
  input  A1,
  input  B1,
  input  A0_2,
  input  A1_2,
  output P0,
  output P1,
  output P3,
  output P2
);

  wire and_1_out, and_2_out, and_3_out, meio_somador_2_c;

  and and_1 (and_1_out, A1_2, B1);
  meio_somador meio_somador_1 (.A(meio_somador_2_c), .B(and_1_out), .S(P2), .C(P3));
  and and_2 (and_2_out, A0_2, B1);
  meio_somador meio_somador_2 (.A(and_3_out), .B(and_2_out), .S(P1), .C(meio_somador_2_c));
  and and_3 (and_3_out, B0, A1);
  and and_4 (P0, B0, A0);
endmodule
