// Digital circuit multiplicador3bits.dig as structural Verilog
module multiplicador3bits (
  input  B0,
  input  A0,
  input  A1,
  input  B1,
  input  A0_2,
  input  A1_2,
  input  A2,
  input  B2,
  input  A2_2,
  input  A0_3,
  input  A1_3,
  input  A2_3,
  output P0,
  output P1,
  output P2,
  output P3,
  output P4,
  output P5
);

  wire and_1_out, and_2_out, and_3_out, and_4_out, and_5_out, and_6_out, and_7_out, and_8_out,
       meio_somador_1_c, meio_somador_1_s, meio_somador_2_c, meio_somador_3_c, somador1bit_2_cout,
       somador1bit_3_cout, somador1bit_3_s;

  and and_1 (and_1_out, A2_3, B2);
  somador1bit somador1bit_1 (.A(somador1bit_2_cout), .B(and_1_out), .Cin(meio_somador_1_c), .S(P4), .Cout(P5));
  and and_2 (and_2_out, A2_2, B1);
  meio_somador meio_somador_1 (.A(somador1bit_3_cout), .B(and_2_out), .S(meio_somador_1_s), .C(meio_somador_1_c));
  and and_3 (and_3_out, A1_3, B2);
  somador1bit somador1bit_2 (
    .A(meio_somador_2_c), .B(and_3_out), .Cin(meio_somador_1_s), .S(P3), .Cout(somador1bit_2_cout));
  and and_4 (and_4_out, A1_2, B1);
  somador1bit somador1bit_3 (
    .A(meio_somador_3_c), .B(and_5_out), .Cin(and_4_out), .S(somador1bit_3_s), .Cout(somador1bit_3_cout));
  and and_5 (and_5_out, B0, A2);
  and and_6 (and_6_out, A0_3, B2);
  meio_somador meio_somador_2 (.A(and_6_out), .B(somador1bit_3_s), .S(P2), .C(meio_somador_2_c));
  and and_7 (and_7_out, A0_2, B1);
  meio_somador meio_somador_3 (.A(and_8_out), .B(and_7_out), .S(P1), .C(meio_somador_3_c));
  and and_8 (and_8_out, B0, A1);
  and and_9 (P0, B0, A0);
endmodule
