// Digital circuit multiplicador8bits.dig as structural Verilog
module multiplicador8bits (
  input  A0,
  input  A1,
  input  A2,
  input  A3,
  input  A4,
  input  A5,
  input  A6,
  input  A7,
  input  B0,
  input  B1,
  input  A0_2,
  input  A1_2,
  input  A2_2,
  input  A3_2,
  input  A4_2,
  input  A5_2,
  input  A6_2,
  input  A7_2,
  input  B2,
  input  A0_3,
  input  A1_3,
  input  A2_3,
  input  A3_3,
  input  A4_3,
  input  A5_3,
  input  A6_3,
  input  A7_3,
  input  B3,
  input  A0_4,
  input  A1_4,
  input  A2_4,
  input  A3_4,
  input  A4_4,
  input  A5_4,
  input  A6_4,
  input  A7_4,
  input  B4,
  input  A0_5,
  input  A1_5,
  input  A2_5,
  input  A3_5,
  input  A4_5,
  input  A5_5,
  input  A6_5,
  input  A7_5,
  input  B5,
  input  A0_6,
  input  A1_6,
  input  A2_6,
  input  A3_6,
  input  A4_6,
  input  A5_6,
  input  A6_6,
  input  A7_6,
  input  B6,
  input  A0_7,
  input  A1_7,
  input  A2_7,
  input  A3_7,
  input  A4_7,
  input  A5_7,
  input  A6_7,
  input  A7_7,
  input  B7,
  input  A0_8,
  input  A1_8,
  input  A2_8,
  input  A3_8,
  input  A4_8,
  input  A5_8,
  input  A6_8,
  input  A7_8,
  output P15,
  output P14,
  output P13,
  output P12,
  output P11,
  output P10,
  output P9,
  output P8,
  output P7,
  output P6,
  output P5,
  output P4,
  output P3,
  output P2,
  output P1,
  output P0
);

  wire and_1_out, and_2_out, and_3_out, and_4_out, and_5_out, and_6_out, and_7_out, and_8_out, and_9_out,
       and_10_out, and_11_out, and_12_out, and_13_out, and_14_out, and_15_out, and_16_out, and_17_out,
       and_18_out, and_19_out, and_20_out, and_21_out, and_22_out, and_23_out, and_24_out, and_25_out,
       and_26_out, and_27_out, and_28_out, and_29_out, and_30_out, and_31_out, and_32_out, and_33_out,
       and_34_out, and_35_out, and_36_out, and_37_out, and_38_out, and_39_out, and_40_out, and_41_out,
       and_42_out, and_43_out, and_44_out, and_45_out, and_46_out, and_47_out, and_48_out, and_49_out,
       and_50_out, and_51_out, and_52_out, and_53_out, and_54_out, and_55_out, and_56_out, and_57_out,
       and_58_out, and_59_out, and_60_out, and_61_out, and_62_out, and_63_out, meio_somador_1_c,
       meio_somador_1_s, meio_somador_2_c, meio_somador_3_c, meio_somador_4_c, meio_somador_5_c,
       meio_somador_6_c, meio_somador_7_c, meio_somador_8_c, somador1bit_2_cout, somador1bit_3_cout,
       somador1bit_3_s, somador1bit_4_cout, somador1bit_4_s, somador1bit_5_cout, somador1bit_6_cout,
       somador1bit_6_s, somador1bit_7_cout, somador1bit_7_s, somador1bit_8_cout, somador1bit_8_s,
       somador1bit_9_cout, somador1bit_9_s, somador1bit_10_cout, somador1bit_11_cout, somador1bit_11_s,
       somador1bit_12_cout, somador1bit_12_s, somador1bit_13_cout, somador1bit_13_s, somador1bit_14_cout,
       somador1bit_15_cout, somador1bit_15_s, somador1bit_16_cout, somador1bit_16_s, somador1bit_17_cout,
       somador1bit_18_cout, somador1bit_18_s, somador1bit_19_cout, somador1bit_19_s, somador1bit_20_cout,
       somador1bit_20_s, somador1bit_21_cout, somador1bit_21_s, somador1bit_22_cout, somador1bit_22_s,
       somador1bit_23_cout, somador1bit_23_s, somador1bit_24_cout, somador1bit_25_cout, somador1bit_25_s,
       somador1bit_26_cout, somador1bit_26_s, somador1bit_27_cout, somador1bit_27_s, somador1bit_28_cout,
       somador1bit_28_s, somador1bit_29_cout, somador1bit_29_s, somador1bit_30_cout, somador1bit_30_s,
       somador1bit_31_cout, somador1bit_31_s, somador1bit_32_cout, somador1bit_32_s, somador1bit_33_cout,
       somador1bit_33_s, somador1bit_34_cout, somador1bit_34_s, somador1bit_35_cout, somador1bit_35_s,
       somador1bit_36_cout, somador1bit_36_s, somador1bit_37_cout, somador1bit_37_s, somador1bit_38_cout,
       somador1bit_38_s, somador1bit_39_cout, somador1bit_39_s, somador1bit_40_cout, somador1bit_40_s,
       somador1bit_41_cout, somador1bit_41_s, somador1bit_42_cout, somador1bit_42_s, somador1bit_43_cout,
       somador1bit_43_s, somador1bit_44_cout, somador1bit_44_s, somador1bit_45_cout, somador1bit_45_s,
       somador1bit_46_cout, somador1bit_46_s, somador1bit_47_cout, somador1bit_47_s, somador1bit_48_cout,
       somador1bit_48_s;

  and and_1 (and_1_out, A7_8, B7);
  somador1bit somador1bit_1 (.A(somador1bit_2_cout), .B(somador1bit_3_cout), .Cin(and_1_out), .S(P14), .Cout(P15));
  and and_2 (and_2_out, A7_7, B6);
  and and_3 (and_3_out, A6_8, B7);
  somador1bit somador1bit_2 (
    .A(somador1bit_5_cout), .B(somador1bit_3_s), .Cin(and_3_out), .S(P13), .Cout(somador1bit_2_cout));
  somador1bit somador1bit_3 (
    .A(somador1bit_4_cout), .B(somador1bit_6_cout), .Cin(and_2_out), .S(somador1bit_3_s),
    .Cout(somador1bit_3_cout));
  and and_4 (and_4_out, A7_6, B5);
  and and_5 (and_5_out, A6_7, B6);
  somador1bit somador1bit_4 (
    .A(somador1bit_9_cout), .B(somador1bit_6_s), .Cin(and_5_out), .S(somador1bit_4_s),
    .Cout(somador1bit_4_cout));
  and and_6 (and_6_out, A5_8, B7);
  somador1bit somador1bit_5 (
    .A(somador1bit_10_cout), .B(somador1bit_4_s), .Cin(and_6_out), .S(P12), .Cout(somador1bit_5_cout));
  somador1bit somador1bit_6 (
    .A(somador1bit_8_cout), .B(somador1bit_7_cout), .Cin(and_4_out), .S(somador1bit_6_s),
    .Cout(somador1bit_6_cout));
  and and_7 (and_7_out, A4_8, B7);
  and and_8 (and_8_out, A7_5, B4);
  somador1bit somador1bit_7 (
    .A(somador1bit_11_cout), .B(somador1bit_15_cout), .Cin(and_8_out), .S(somador1bit_7_s),
    .Cout(somador1bit_7_cout));
  and and_9 (and_9_out, A6_6, B5);
  somador1bit somador1bit_8 (
    .A(somador1bit_12_cout), .B(somador1bit_7_s), .Cin(and_9_out), .S(somador1bit_8_s),
    .Cout(somador1bit_8_cout));
  and and_10 (and_10_out, A5_7, B6);
  somador1bit somador1bit_9 (
    .A(somador1bit_13_cout), .B(somador1bit_8_s), .Cin(and_10_out), .S(somador1bit_9_s),
    .Cout(somador1bit_9_cout));
  somador1bit somador1bit_10 (
    .A(somador1bit_14_cout), .B(somador1bit_9_s), .Cin(and_7_out), .S(P11), .Cout(somador1bit_10_cout));
  and and_11 (and_11_out, A3_8, B7);
  and and_12 (and_12_out, A7_4, B3);
  and and_13 (and_13_out, A6_5, B4);
  somador1bit somador1bit_11 (
    .A(somador1bit_19_cout), .B(somador1bit_15_s), .Cin(and_13_out), .S(somador1bit_11_s),
    .Cout(somador1bit_11_cout));
  and and_14 (and_14_out, A5_6, B5);
  somador1bit somador1bit_12 (
    .A(somador1bit_20_cout), .B(somador1bit_11_s), .Cin(and_14_out), .S(somador1bit_12_s),
    .Cout(somador1bit_12_cout));
  and and_15 (and_15_out, A4_7, B6);
  somador1bit somador1bit_13 (
    .A(somador1bit_21_cout), .B(somador1bit_12_s), .Cin(and_15_out), .S(somador1bit_13_s),
    .Cout(somador1bit_13_cout));
  somador1bit somador1bit_14 (
    .A(somador1bit_17_cout), .B(somador1bit_13_s), .Cin(and_11_out), .S(P10), .Cout(somador1bit_14_cout));
  somador1bit somador1bit_15 (
    .A(somador1bit_18_cout), .B(somador1bit_16_cout), .Cin(and_12_out), .S(somador1bit_15_s),
    .Cout(somador1bit_15_cout));
  and and_16 (and_16_out, A7_3, B2);
  somador1bit somador1bit_16 (
    .A(somador1bit_22_cout), .B(meio_somador_1_c), .Cin(and_16_out), .S(somador1bit_16_s),
    .Cout(somador1bit_16_cout));
  and and_17 (and_17_out, A3_7, B6);
  and and_18 (and_18_out, A2_8, B7);
  somador1bit somador1bit_17 (
    .A(somador1bit_24_cout), .B(somador1bit_21_s), .Cin(and_18_out), .S(P9), .Cout(somador1bit_17_cout));
  and and_19 (and_19_out, A6_4, B3);
  somador1bit somador1bit_18 (
    .A(somador1bit_25_cout), .B(and_19_out), .Cin(somador1bit_16_s), .S(somador1bit_18_s),
    .Cout(somador1bit_18_cout));
  and and_20 (and_20_out, A5_5, B4);
  somador1bit somador1bit_19 (
    .A(somador1bit_26_cout), .B(somador1bit_18_s), .Cin(and_20_out), .S(somador1bit_19_s),
    .Cout(somador1bit_19_cout));
  and and_21 (and_21_out, A4_6, B5);
  somador1bit somador1bit_20 (
    .A(somador1bit_27_cout), .B(somador1bit_19_s), .Cin(and_21_out), .S(somador1bit_20_s),
    .Cout(somador1bit_20_cout));
  somador1bit somador1bit_21 (
    .A(somador1bit_23_cout), .B(somador1bit_20_s), .Cin(and_17_out), .S(somador1bit_21_s),
    .Cout(somador1bit_21_cout));
  and and_22 (and_22_out, A6_3, B2);
  and and_23 (and_23_out, A7_2, B1);
  meio_somador meio_somador_1 (.A(somador1bit_29_cout), .B(and_23_out), .S(meio_somador_1_s), .C(meio_somador_1_c));
  somador1bit somador1bit_22 (
    .A(somador1bit_28_cout), .B(meio_somador_1_s), .Cin(and_22_out), .S(somador1bit_22_s),
    .Cout(somador1bit_22_cout));
  and and_24 (and_24_out, A3_6, B5);
  and and_25 (and_25_out, A2_7, B6);
  somador1bit somador1bit_23 (
    .A(somador1bit_31_cout), .B(somador1bit_27_s), .Cin(and_25_out), .S(somador1bit_23_s),
    .Cout(somador1bit_23_cout));
  and and_26 (and_26_out, A1_8, B7);
  somador1bit somador1bit_24 (
    .A(meio_somador_2_c), .B(somador1bit_23_s), .Cin(and_26_out), .S(P8), .Cout(somador1bit_24_cout));
  and and_27 (and_27_out, A5_4, B3);
  somador1bit somador1bit_25 (
    .A(somador1bit_32_cout), .B(and_27_out), .Cin(somador1bit_22_s), .S(somador1bit_25_s),
    .Cout(somador1bit_25_cout));
  and and_28 (and_28_out, A4_5, B4);
  somador1bit somador1bit_26 (
    .A(somador1bit_33_cout), .B(somador1bit_25_s), .Cin(and_28_out), .S(somador1bit_26_s),
    .Cout(somador1bit_26_cout));
  somador1bit somador1bit_27 (
    .A(somador1bit_30_cout), .B(somador1bit_26_s), .Cin(and_24_out), .S(somador1bit_27_s),
    .Cout(somador1bit_27_cout));
  and and_29 (and_29_out, A5_3, B2);
  somador1bit somador1bit_28 (
    .A(somador1bit_34_cout), .B(somador1bit_29_s), .Cin(and_29_out), .S(somador1bit_28_s),
    .Cout(somador1bit_28_cout));
  and and_30 (and_30_out, A6_2, B1);
  somador1bit somador1bit_29 (
    .A(somador1bit_35_cout), .B(and_35_out), .Cin(and_30_out), .S(somador1bit_29_s),
    .Cout(somador1bit_29_cout));
  and and_31 (and_31_out, A3_5, B4);
  and and_32 (and_32_out, A2_6, B5);
  somador1bit somador1bit_30 (
    .A(somador1bit_38_cout), .B(somador1bit_33_s), .Cin(and_32_out), .S(somador1bit_30_s),
    .Cout(somador1bit_30_cout));
  and and_33 (and_33_out, A1_7, B6);
  somador1bit somador1bit_31 (
    .A(meio_somador_3_c), .B(somador1bit_30_s), .Cin(and_33_out), .S(somador1bit_31_s),
    .Cout(somador1bit_31_cout));
  and and_34 (and_34_out, A0_8, B7);
  meio_somador meio_somador_2 (.A(somador1bit_31_s), .B(and_34_out), .S(P7), .C(meio_somador_2_c));
  and and_35 (and_35_out, B0, A7);
  and and_36 (and_36_out, A4_4, B3);
  somador1bit somador1bit_32 (
    .A(somador1bit_36_cout), .B(and_36_out), .Cin(somador1bit_28_s), .S(somador1bit_32_s),
    .Cout(somador1bit_32_cout));
  somador1bit somador1bit_33 (
    .A(somador1bit_37_cout), .B(somador1bit_32_s), .Cin(and_31_out), .S(somador1bit_33_s),
    .Cout(somador1bit_33_cout));
  and and_37 (and_37_out, A4_3, B2);
  somador1bit somador1bit_34 (
    .A(somador1bit_39_cout), .B(somador1bit_35_s), .Cin(and_37_out), .S(somador1bit_34_s),
    .Cout(somador1bit_34_cout));
  and and_38 (and_38_out, A5_2, B1);
  somador1bit somador1bit_35 (
    .A(somador1bit_40_cout), .B(and_41_out), .Cin(and_38_out), .S(somador1bit_35_s),
    .Cout(somador1bit_35_cout));
  and and_39 (and_39_out, A1_6, B5);
  and and_40 (and_40_out, A0_7, B6);
  meio_somador meio_somador_3 (.A(somador1bit_38_s), .B(and_40_out), .S(P6), .C(meio_somador_3_c));
  and and_41 (and_41_out, B0, A6);
  and and_42 (and_42_out, A3_4, B3);
  somador1bit somador1bit_36 (
    .A(somador1bit_42_cout), .B(and_42_out), .Cin(somador1bit_34_s), .S(somador1bit_36_s),
    .Cout(somador1bit_36_cout));
  and and_43 (and_43_out, A2_5, B4);
  somador1bit somador1bit_37 (
    .A(somador1bit_41_cout), .B(somador1bit_36_s), .Cin(and_43_out), .S(somador1bit_37_s),
    .Cout(somador1bit_37_cout));
  somador1bit somador1bit_38 (
    .A(meio_somador_4_c), .B(somador1bit_37_s), .Cin(and_39_out), .S(somador1bit_38_s),
    .Cout(somador1bit_38_cout));
  and and_44 (and_44_out, A3_3, B2);
  somador1bit somador1bit_39 (
    .A(somador1bit_43_cout), .B(somador1bit_40_s), .Cin(and_44_out), .S(somador1bit_39_s),
    .Cout(somador1bit_39_cout));
  and and_45 (and_45_out, A4_2, B1);
  somador1bit somador1bit_40 (
    .A(somador1bit_44_cout), .B(and_48_out), .Cin(and_45_out), .S(somador1bit_40_s),
    .Cout(somador1bit_40_cout));
  and and_46 (and_46_out, A1_5, B4);
  somador1bit somador1bit_41 (
    .A(meio_somador_5_c), .B(somador1bit_42_s), .Cin(and_46_out), .S(somador1bit_41_s),
    .Cout(somador1bit_41_cout));
  and and_47 (and_47_out, A0_6, B5);
  meio_somador meio_somador_4 (.A(somador1bit_41_s), .B(and_47_out), .S(P5), .C(meio_somador_4_c));
  and and_48 (and_48_out, B0, A5);
  and and_49 (and_49_out, A2_4, B3);
  somador1bit somador1bit_42 (
    .A(somador1bit_45_cout), .B(and_49_out), .Cin(somador1bit_39_s), .S(somador1bit_42_s),
    .Cout(somador1bit_42_cout));
  and and_50 (and_50_out, A2_3, B2);
  somador1bit somador1bit_43 (
    .A(somador1bit_46_cout), .B(somador1bit_44_s), .Cin(and_50_out), .S(somador1bit_43_s),
    .Cout(somador1bit_43_cout));
  and and_51 (and_51_out, A3_2, B1);
  somador1bit somador1bit_44 (
    .A(somador1bit_47_cout), .B(and_52_out), .Cin(and_51_out), .S(somador1bit_44_s),
    .Cout(somador1bit_44_cout));
  and and_52 (and_52_out, B0, A4);
  and and_53 (and_53_out, A1_4, B3);
  somador1bit somador1bit_45 (
    .A(meio_somador_6_c), .B(and_53_out), .Cin(somador1bit_43_s), .S(somador1bit_45_s),
    .Cout(somador1bit_45_cout));
  and and_54 (and_54_out, A1_3, B2);
  meio_somador meio_somador_5 (.A(and_55_out), .B(somador1bit_45_s), .S(P4), .C(meio_somador_5_c));
  somador1bit somador1bit_46 (
    .A(meio_somador_7_c), .B(somador1bit_47_s), .Cin(and_54_out), .S(somador1bit_46_s),
    .Cout(somador1bit_46_cout));
  and and_55 (and_55_out, A0_5, B4);
  and and_56 (and_56_out, A2_2, B1);
  somador1bit somador1bit_47 (
    .A(somador1bit_48_cout), .B(and_57_out), .Cin(and_56_out), .S(somador1bit_47_s),
    .Cout(somador1bit_47_cout));
  and and_57 (and_57_out, B0, A3);
  and and_58 (and_58_out, A0_4, B3);
  meio_somador meio_somador_6 (.A(and_58_out), .B(somador1bit_46_s), .S(P3), .C(meio_somador_6_c));
  and and_59 (and_59_out, A1_2, B1);
  somador1bit somador1bit_48 (
    .A(meio_somador_8_c), .B(and_61_out), .Cin(and_59_out), .S(somador1bit_48_s), .Cout(somador1bit_48_cout));
  and and_60 (and_60_out, A0_3, B2);
  meio_somador meio_somador_7 (.A(somador1bit_48_s), .B(and_60_out), .S(P2), .C(meio_somador_7_c));
  and and_61 (and_61_out, B0, A2);
  and and_62 (and_62_out, A0_2, B1);
  meio_somador meio_somador_8 (.A(and_63_out), .B(and_62_out), .S(P1), .C(meio_somador_8_c));
  and and_63 (and_63_out, B0, A1);
  and and_64 (P0, B0, A0);
endmodule
