// Digital circuit somador8bits.dig as structural Verilog
module somador8bits (
  input  A,
  input  B,
  input  A_2,
  input  B_2,
  input  A_3,
  input  B_3,
  input  A_4,
  input  B_4,
  input  A_5,
  input  B_5,
  input  A_6,
  input  B_6,
  input  A_7,
  input  B_7,
  input  A_8,
  input  B_8,
  output S,
  output S_2,
  output S_3,
  output S_4,
  output S_5,
  output S_6,
  output S_7,
  output S_8,
  output Cout
);

  wire and_1_out, and_2_out, and_3_out, and_4_out, and_5_out, and_6_out, and_7_out, and_8_out, and_9_out,
       and_10_out, and_11_out, and_12_out, and_13_out, and_14_out, and_15_out, and_16_out, or_2_out,
       or_3_out, or_4_out, or_5_out, or_6_out, or_7_out, or_8_out, xor_1_out, xor_3_out, xor_5_out,
       xor_7_out, xor_9_out, xor_11_out, xor_13_out, xor_15_out;

  xor xor_1 (xor_1_out, A_8, B_8);
  and and_1 (and_1_out, A_8, B_8);
  xor xor_2 (S_8, xor_1_out, or_2_out);
  and and_2 (and_2_out, xor_1_out, or_2_out);
  or or_1 (Cout, and_2_out, and_1_out);
  xor xor_3 (xor_3_out, A_7, B_7);
  and and_3 (and_3_out, A_7, B_7);
  xor xor_4 (S_7, xor_3_out, or_3_out);
  and and_4 (and_4_out, xor_3_out, or_3_out);
  or or_2 (or_2_out, and_4_out, and_3_out);
  xor xor_5 (xor_5_out, A_6, B_6);
  and and_5 (and_5_out, A_6, B_6);
  xor xor_6 (S_6, xor_5_out, or_4_out);
  and and_6 (and_6_out, xor_5_out, or_4_out);
  or or_3 (or_3_out, and_6_out, and_5_out);
  xor xor_7 (xor_7_out, A_5, B_5);
  and and_7 (and_7_out, A_5, B_5);
  xor xor_8 (S_5, xor_7_out, or_5_out);
  and and_8 (and_8_out, xor_7_out, or_5_out);
  or or_4 (or_4_out, and_8_out, and_7_out);
  xor xor_9 (xor_9_out, A_4, B_4);
  and and_9 (and_9_out, A_4, B_4);
  xor xor_10 (S_4, xor_9_out, or_6_out);
  and and_10 (and_10_out, xor_9_out, or_6_out);
  or or_5 (or_5_out, and_10_out, and_9_out);
  xor xor_11 (xor_11_out, A_3, B_3);
  and and_11 (and_11_out, A_3, B_3);
  xor xor_12 (S_3, xor_11_out, or_7_out);
  and and_12 (and_12_out, xor_11_out, or_7_out);
  or or_6 (or_6_out, and_12_out, and_11_out);
  xor xor_13 (xor_13_out, A_2, B_2);
  and and_13 (and_13_out, A_2, B_2);
  xor xor_14 (S_2, xor_13_out, or_8_out);
  and and_14 (and_14_out, xor_13_out, or_8_out);
  or or_7 (or_7_out, and_14_out, and_13_out);
  xor xor_15 (xor_15_out, A, B);
  and and_15 (and_15_out, A, B);
  xor xor_16 (S, xor_15_out, 1'b0);
  and and_16 (and_16_out, xor_15_out, 1'b0);
  or or_8 (or_8_out, and_16_out, and_15_out);
endmodule
