// Digital circuit alu.dig as structural Verilog
module alu (
  input  [7:0] A,
  input  [7:0] B,
  input  [1:0] Sel
);

  wire [7:0] subtrator8bits_1_p1;

  // subtrator8bits subtrator8bits_1: pin names not known; wires that end beside it: subtrator8bits_1_p1, subtrator8bits_1_p1, subtrator8bits_1_p1, subtrator8bits_1_p1, subtrator8bits_1_p1, subtrator8bits_1_p1, subtrator8bits_1_p1, subtrator8bits_1_p1
  multiplicador8bits multiplicador8bits_1 ();  // open: A0, A1, A2, A3, A4, A5, A6, A7, B0, B1, A0_2, A1_2, A2_2, A3_2, A4_2, A5_2, A6_2, A7_2, B2, A0_3, A1_3, A2_3, A3_3, A4_3, A5_3, A6_3, A7_3, B3, A0_4, A1_4, A2_4, A3_4, A4_4, A5_4, A6_4, A7_4, B4, A0_5, A1_5, A2_5, A3_5, A4_5, A5_5, A6_5, A7_5, B5, A0_6, A1_6, A2_6, A3_6, A4_6, A5_6, A6_6, A7_6, B6, A0_7, A1_7, A2_7, A3_7, A4_7, A5_7, A6_7, A7_7, B7, A0_8, A1_8, A2_8, A3_8, A4_8, A5_8, A6_8, A7_8, P15, P14, P13, P12, P11, P10, P9, P8, P7, P6, P5, P4, P3, P2, P1, P0
endmodule
