// Digital circuit alu8bits.dig as structural Verilog
module alu8bits (
  input  [7:0] N,
  input  [2:0] S,
  input  CLK,
  output [7:0] MQ,
  output neg,
  output [7:0] AC,
  output Over
);

  wire neg_t, Over_t, sMQ;
  wire [7:0] _000, _001, _010, _011, _100, _101, _110, _111, MQ0, MQ1, multiplexer_1_out, multiplexer_2_out;

  Multiplexer #(.Bits(8)) multiplexer_1 (.sel(sMQ), .in_0(MQ0), .in_1(MQ1), .out(multiplexer_1_out));
  Register #(.Bits(8)) u_AC (.D(multiplexer_2_out), .C(CLK), .en(1'b1), .Q(AC));
  and and_1 (sMQ, S[0], S[1], ~S[2]);  // And
  Register #(.Bits(8)) u_MQ (.D(multiplexer_1_out), .C(CLK), .en(1'b1), .Q(MQ));
  Multiplexer #(.Selector_Bits(3), .Bits(8)) multiplexer_2 (
    .sel(S), .in_0(_000), .in_1(_001), .in_2(_010), .in_3(_011), .in_4(_100), .in_5(_101), .in_6(_110),
    .in_7(_111), .out(multiplexer_2_out));
  and and_2 (Over, Over_t, ~S[0], ~S[1], ~S[2]);  // And
  and and_3 (neg, neg_t, S[0], ~S[1], ~S[2]);  // And
  xor8bits xor8bits_1 (.A(AC), .N(N), .ACout(_111));
  nand8bits nand8bits_1 (.A(AC), .N(N), .ACout(_110));
  shift_esq shift_esq_1 (.A(AC), .Cout(_101));
  shift_dir shift_dir_1 (.A(AC), .Cout(_100));
  somador somador_1 (.AC(AC), .N(N), .S(_000), .Overflow(Over_t));
  subtrator subtrator_1 (.AC(AC), .N(N), .S(_001), .Overflow(neg_t));
  multiplicador multiplicador_1 (.AC(AC), .B(N), .ACout(_010), .MQout(MQ0));
  divisor8bits divisor8bits_1 (.A(AC), .B(N), .Q(_011), .Resto(MQ1));

  // Other names for the same wires on the sheet: sAC[2:0] = S
endmodule
