// Digital circuit contador4bits.dig as structural Verilog
module contador4bits (
  input  Set,
  input  CLK,
  input  Clr,
  output [3:0] O
);

  wire jk_ff_as_1_nq, jk_ff_as_2_nq, jk_ff_as_3_nq;

  JK_FF_AS jk_ff_as_1 (.Set(Set), .J(1'b1), .C(CLK), .K(1'b1), .Clr(Clr), .Q(O[0]), .nQ(jk_ff_as_1_nq));
  JK_FF_AS jk_ff_as_2 (.Set(1'b0), .J(1'b1), .C(jk_ff_as_1_nq), .K(1'b1), .Clr(Clr), .Q(O[1]), .nQ(jk_ff_as_2_nq));
  JK_FF_AS jk_ff_as_3 (.Set(1'b0), .J(1'b1), .C(jk_ff_as_2_nq), .K(1'b1), .Clr(Clr), .Q(O[2]), .nQ(jk_ff_as_3_nq));
  JK_FF_AS jk_ff_as_4 (.Set(1'b0), .J(1'b1), .C(jk_ff_as_3_nq), .K(1'b1), .Clr(Clr), .Q(O[3]));  // open: nQ
endmodule
