// Digital circuit contador_de_anel4bits.dig as structural Verilog
module contador_de_anel4bits (
  input  CLK,
  input  Set,
  output O0,
  output O1,
  output O2,
  output O3
);

  wire or_1_out;

  or or_1 (or_1_out, O3, Set);
  D_FF d_ff_1 (.D(or_1_out), .C(~CLK), .Q(O0));  // open: nQ
  D_FF d_ff_2 (.D(O0), .C(~CLK), .Q(O1));  // open: nQ
  D_FF d_ff_3 (.D(O1), .C(~CLK), .Q(O2));  // open: nQ
  D_FF d_ff_4 (.D(O2), .C(~CLK), .Q(O3));  // open: nQ
endmodule
