// Digital circuit cpu8bits.dig as structural Verilog
module cpu8bits (
  input  in_12,
  output [3:0] out_1,
  output [3:0] out_2,
  output [7:0] out_3,
  output [7:0] out_4,
  output [4:0] out_5,
  output [7:0] out_6,
  output [2:0] out_7,
  output [2:0] out_8,
  output [7:0] out_9,
  output [7:0] MQ,
  output [7:0] AC
);

  wire AC_LOAD, B, CLK, CLK_PC, IR_LOAD, MAR;
  wire [3:0] driver_3_out, MAR_q;
  wire [7:0] driver_2_out, driver_7_out;

  contador4bits contador4bits_1 (.Set(1'b0), .CLK(CLK_PC), .Clr(in_12), .O(out_1));
  and and_1 (CLK_PC, IR_LOAD, CLK);
  Button button_1 (.out(CLK));
  assign out_4 = IR_LOAD ? driver_2_out : 8'bz;  // Driver driver_1
  contador_de_anel4bits contador_de_anel4bits_1 (.CLK(CLK), .Set(in_12), .O0(MAR), .O1(IR_LOAD), .O2(B), .O3(AC_LOAD));
  assign driver_2_out = MAR ? {4'b0000, out_1} : 8'bz;  // Driver driver_2
  Register #(.Bits(8)) IR (.D(out_4), .C(CLK), .en(IR_LOAD), .Q({out_8, out_5}));
  assign {out_2, driver_3_out} = MAR ? driver_2_out : 8'bz;  // Driver driver_3
  Register #(.Bits(4)) u_MAR (.D(driver_3_out), .C(CLK), .en(MAR), .Q(MAR_q));
  EEPROMDualPort #(.AddrBits(5), .Bits(8)) operandos (
    .A(out_5), .Din({8{1'b0}}), .str(1'b0), .C(CLK), .ld(B), .D(out_6));
  EEPROMDualPort #(.AddrBits(4), .Bits(8)) \operações  (
    .A(MAR_q), .Din({8{1'b0}}), .str(1'b0), .C(CLK), .ld(IR_LOAD), .D(out_3));
  assign driver_2_out = B ? out_6 : 8'bz;  // Driver driver_4
  assign out_7 = AC_LOAD ? out_8 : 3'bz;  // Driver driver_5
  assign driver_2_out = IR_LOAD ? out_3 : 8'bz;  // Driver driver_6
  assign driver_7_out = B ? driver_2_out : 8'bz;  // Driver driver_7
  Register #(.Bits(8)) register_1 (.D(driver_7_out), .C(CLK), .en(B), .Q(out_9));
  alu8bits alu8bits_1 (.N(out_9), .S(out_7), .CLK(CLK), .MQ(MQ), .AC(AC));  // open: neg, Over

  // Other names for the same wires on the sheet: ALU = AC_LOAD; CLR = in_12; operando_EN = B; operações_EN = IR_LOAD;
  //   PC_INT = IR_LOAD; PC_EN = MAR
endmodule
