// Digital circuit multiplicador.dig as structural Verilog
module multiplicador (
  input  [7:0] AC,
  input  [7:0] B,
  output [7:0] ACout,
  output [7:0] MQout
);

  wire A0B1, A0B2, A0B3, A0B4, A0B5, A0B6, A0B7, A1B0, A1B1, A1B2, A1B3, A1B4, A1B5, A1B6, A1B7, A2B0, A2B1,
       A2B2, A2B3, A2B4, A2B5, A2B6, A2B7, A3B0, A3B1, A3B2, A3B3, A3B4, A3B5, A3B6, A3B7, A4B0, A4B1, A4B2,
       A4B3, A4B4, A4B5, A4B6, A4B7, A5B0, A5B1, A5B2, A5B3, A5B4, A5B5, A5B6, A5B7, A6B0, A6B1, A6B2, A6B3,
       A6B4, A6B5, A6B6, A6B7, A7B0, A7B1, A7B2, A7B3, A7B4, A7B5, A7B6, A7B7, Cout0, Cout1, Cout2, Cout3,
       Cout4, Cout5, Cout6, Cout7, Cout8, Cout9, Cout10, Cout11, Cout12, Cout13, Cout14, Cout15, Cout16,
       Cout17, Cout18, Cout19, Cout20, Cout21, Cout22, Cout23, Cout24, Cout25, Cout26, Cout27, Cout28,
       Cout29, Cout30, Cout31, Cout32, Cout33, Cout34, Cout35, Cout36, Cout37, Cout38, Cout39, Cout40,
       Cout41, Cout42, Cout43, Cout44, Cout45, Cout46, Cout47, Cout48, SP0, SP1, SP2, SP3, SP4, SP5, SP6,
       SP7, SP8, SP9, SP10, SP11, SP12, SP13, SP14, SP15, SP16, SP17, SP18, SP19, SP20, SP21, SP22, SP23,
       SP24, SP25, SP26, SP27, SP28, SP29, SP30, SP31, SP32, SP33, SP34, SP35;

  and and_1 (A7B7, B[7], AC[7]);
  and and_2 (A7B6, B[6], AC[7]);
  and and_3 (A6B7, B[7], AC[6]);
  and and_4 (A7B5, B[5], AC[7]);
  and and_5 (A6B6, B[6], AC[6]);
  and and_6 (A5B7, B[7], AC[5]);
  and and_7 (A7B4, B[4], AC[7]);
  and and_8 (A6B5, B[5], AC[6]);
  and and_9 (A5B6, B[6], AC[5]);
  and and_10 (A4B7, B[7], AC[4]);
  and and_11 (A7B3, B[3], AC[7]);
  and and_12 (A6B4, B[4], AC[6]);
  and and_13 (A5B5, B[5], AC[5]);
  and and_14 (A4B6, B[6], AC[4]);
  and and_15 (A3B7, B[7], AC[3]);
  and and_16 (A7B2, B[2], AC[7]);
  and and_17 (A6B3, B[3], AC[6]);
  and and_18 (A5B4, B[4], AC[5]);
  and and_19 (A4B5, B[5], AC[4]);
  and and_20 (A3B6, B[6], AC[3]);
  and and_21 (A2B7, B[7], AC[2]);
  and and_22 (A7B1, B[1], AC[7]);
  and and_23 (A6B2, B[2], AC[6]);
  and and_24 (A5B3, B[3], AC[5]);
  and and_25 (A4B4, B[4], AC[4]);
  and and_26 (A3B5, B[5], AC[3]);
  and and_27 (A2B6, B[6], AC[2]);
  and and_28 (A1B7, B[7], AC[1]);
  and and_29 (A7B0, B[0], AC[7]);
  and and_30 (A6B1, B[1], AC[6]);
  and and_31 (A5B2, B[2], AC[5]);
  and and_32 (A4B3, B[3], AC[4]);
  and and_33 (A3B4, B[4], AC[3]);
  and and_34 (A2B5, B[5], AC[2]);
  and and_35 (A1B6, B[6], AC[1]);
  and and_36 (A0B7, B[7], AC[0]);
  and and_37 (A6B0, B[0], AC[6]);
  and and_38 (A5B1, B[1], AC[5]);
  and and_39 (A4B2, B[2], AC[4]);
  and and_40 (A3B3, B[3], AC[3]);
  and and_41 (A2B4, B[4], AC[2]);
  and and_42 (A1B5, B[5], AC[1]);
  and and_43 (A0B6, B[6], AC[0]);
  and and_44 (A5B0, B[0], AC[5]);
  and and_45 (A4B1, B[1], AC[4]);
  and and_46 (A3B2, B[2], AC[3]);
  and and_47 (A2B3, B[3], AC[2]);
  and and_48 (A1B4, B[4], AC[1]);
  and and_49 (A0B5, B[5], AC[0]);
  and and_50 (A4B0, B[0], AC[4]);
  and and_51 (A3B1, B[1], AC[3]);
  and and_52 (A2B2, B[2], AC[2]);
  and and_53 (A1B3, B[3], AC[1]);
  and and_54 (A0B4, B[4], AC[0]);
  and and_55 (A3B0, B[0], AC[3]);
  and and_56 (A2B1, B[1], AC[2]);
  and and_57 (A1B2, B[2], AC[1]);
  and and_58 (A0B3, B[3], AC[0]);
  and and_59 (A2B0, B[0], AC[2]);
  and and_60 (A1B1, B[1], AC[1]);
  and and_61 (A0B2, B[2], AC[0]);
  and and_62 (A1B0, B[0], AC[1]);
  and and_63 (A0B1, B[1], AC[0]);
  and and_64 (ACout[0], B[0], AC[0]);
  somador1bit A1B0__plus__A0B1 (.A(A1B0), .B(A0B1), .Cin(1'b0), .S(ACout[1]), .Cout(Cout0));
  somador1bit A2B0__plus__A1B1 (.A(A2B0), .B(A1B1), .Cin(Cout0), .S(SP0), .Cout(Cout1));
  somador1bit A3B0__plus__A2B1 (.A(A3B0), .B(A2B1), .Cin(Cout1), .S(SP1), .Cout(Cout3));
  somador1bit A4B0__plus__A3B1 (.A(A4B0), .B(A3B1), .Cin(Cout3), .S(SP3), .Cout(Cout6));
  somador1bit A5B0__plus__A4B1 (.A(A5B0), .B(A4B1), .Cin(Cout6), .S(SP6), .Cout(Cout10));
  somador1bit A6B0__plus__A5B1 (.A(A6B0), .B(A5B1), .Cin(Cout10), .S(SP10), .Cout(Cout15));
  somador1bit A7B0__plus__A6B1 (.A(A7B0), .B(A6B1), .Cin(Cout15), .S(SP15), .Cout(Cout21));
  somador1bit A7B1__plus__A6B2 (.A(A7B1), .B(A6B2), .Cin(Cout21), .S(SP21), .Cout(Cout28));
  somador1bit A7B2__plus__A6B3 (.A(A7B2), .B(A6B3), .Cin(Cout28), .S(SP26), .Cout(Cout34));
  somador1bit A7B3__plus__A6B4 (.A(A7B3), .B(A6B4), .Cin(Cout34), .S(SP30), .Cout(Cout39));
  somador1bit A7B4__plus__A6B5 (.A(A7B4), .B(A6B5), .Cin(Cout39), .S(SP33), .Cout(Cout43));
  somador1bit A7B5__plus__A6B6 (.A(A7B5), .B(A6B6), .Cin(Cout43), .S(SP35), .Cout(Cout46));
  somador1bit A7B6__plus__A6B7 (.A(A7B6), .B(A6B7), .Cin(Cout46), .S(MQout[5]), .Cout(Cout48));
  somador1bit A7B7__plus__Cout48 (.A(A7B7), .B(Cout48), .Cin(1'b0), .S(MQout[6]), .Cout(MQout[7]));
  somador1bit SP0__plus__A0B2 (.A(A0B2), .B(SP0), .Cin(1'b0), .S(ACout[2]), .Cout(Cout2));
  somador1bit A1B2__plus__SP1 (.A(A1B2), .B(SP1), .Cin(Cout2), .S(SP2), .Cout(Cout4));
  somador1bit A2B2__plus__SP3 (.A(A2B2), .B(SP3), .Cin(Cout4), .S(SP4), .Cout(Cout7));
  somador1bit A3B2__plus__SP6 (.A(A3B2), .B(SP6), .Cin(Cout7), .S(SP7), .Cout(Cout11));
  somador1bit A4B2__plus__SP10 (.A(A4B2), .B(SP10), .Cin(Cout11), .S(SP11), .Cout(Cout16));
  somador1bit A5B2__plus__SP15 (.A(A5B2), .B(SP15), .Cin(Cout16), .S(SP16), .Cout(Cout22));
  somador1bit A5B3__plus__SP21 (.A(A5B3), .B(SP21), .Cin(Cout22), .S(SP22), .Cout(Cout29));
  somador1bit A5B4__plus__SP26 (.A(A5B4), .B(SP26), .Cin(Cout29), .S(SP27), .Cout(Cout35));
  somador1bit A5B5__plus__SP30 (.A(A5B5), .B(SP30), .Cin(Cout35), .S(SP31), .Cout(Cout40));
  somador1bit A5B6__plus__SP33 (.A(A5B6), .B(SP33), .Cin(Cout40), .S(SP34), .Cout(Cout44));
  somador1bit A5B7__plus__SP35 (.A(A5B7), .B(SP35), .Cin(Cout44), .S(MQout[4]), .Cout(Cout47));
  somador1bit A0B3__plus__SP2 (.A(A0B3), .B(SP2), .Cin(1'b0), .S(ACout[3]), .Cout(Cout5));
  somador1bit A1B3__plus__SP4 (.A(A1B3), .B(SP4), .Cin(Cout5), .S(SP5), .Cout(Cout8));
  somador1bit A2B3__plus__SP7 (.A(A2B3), .B(SP7), .Cin(Cout8), .S(SP8), .Cout(Cout12));
  somador1bit A3B3__plus__SP11 (.A(A3B3), .B(SP11), .Cin(Cout12), .S(SP12), .Cout(Cout17));
  somador1bit A4B3__plus__SP16 (.A(A4B3), .B(SP16), .Cin(Cout17), .S(SP17), .Cout(Cout23));
  somador1bit A4B4__plus__SP22 (.A(A4B4), .B(SP22), .Cin(Cout23), .S(SP23), .Cout(Cout30));
  somador1bit A4B5__plus__SP27 (.A(A4B5), .B(SP27), .Cin(Cout30), .S(SP28), .Cout(Cout36));
  somador1bit A4B6__plus__SP31 (.A(A4B6), .B(SP31), .Cin(Cout36), .S(SP32), .Cout(Cout41));
  somador1bit A4B7__plus__SP34 (.A(A4B7), .B(SP34), .Cin(Cout41), .S(MQout[3]), .Cout(Cout45));
  somador1bit A0B4__plus__SP5 (.A(A0B4), .B(SP5), .Cin(1'b0), .S(ACout[4]), .Cout(Cout9));
  somador1bit A1B4__plus__SP8 (.A(A1B4), .B(SP8), .Cin(Cout9), .S(SP9), .Cout(Cout13));
  somador1bit A2B4__plus__SP12 (.A(A2B4), .B(SP12), .Cin(Cout13), .S(SP13), .Cout(Cout18));
  somador1bit A3B4__plus__SP17 (.A(A3B4), .B(SP17), .Cin(Cout18), .S(SP18), .Cout(Cout24));
  somador1bit A3B5__plus__SP23 (.A(A3B5), .B(SP23), .Cin(Cout24), .S(SP24), .Cout(Cout31));
  somador1bit A3B6__plus__SP28 (.A(A3B6), .B(SP28), .Cin(Cout31), .S(SP29), .Cout(Cout37));
  somador1bit A3B7__plus__SP32 (.A(A3B7), .B(SP32), .Cin(Cout37), .S(MQout[2]), .Cout(Cout42));
  somador1bit A0B5__plus__SP9 (.A(A0B5), .B(SP9), .Cin(1'b0), .S(ACout[5]), .Cout(Cout14));
  somador1bit A1B5__plus__SP13 (.A(A1B5), .B(SP13), .Cin(Cout14), .S(SP14), .Cout(Cout19));
  somador1bit A2B5__plus__SP18 (.A(A2B5), .B(SP18), .Cin(Cout19), .S(SP19), .Cout(Cout25));
  somador1bit A2B6__plus__SP24 (.A(A2B6), .B(SP24), .Cin(Cout25), .S(SP25), .Cout(Cout32));
  somador1bit A2B7__plus__SP29 (.A(A2B7), .B(SP29), .Cin(Cout32), .S(MQout[1]), .Cout(Cout38));
  somador1bit A0B6__plus__SP14 (.A(A0B6), .B(SP14), .Cin(1'b0), .S(ACout[6]), .Cout(Cout20));
  somador1bit A1B6__plus__SP19 (.A(A1B6), .B(SP19), .Cin(Cout20), .S(SP20), .Cout(Cout26));
  somador1bit A1B7__plus__SP25 (.A(A1B7), .B(SP25), .Cin(Cout26), .S(MQout[0]), .Cout(Cout33));
  somador1bit A0B7__plus__SP20 (.A(A0B7), .B(SP20), .Cin(1'b0), .S(ACout[7]), .Cout(Cout27));

  // Other names for the same wires on the sheet: A0 = AC[0]; A1 = AC[1]; A2 = AC[2]; A3 = AC[3]; A4 = AC[4];
  //   A5 = AC[5]; A6 = AC[6]; A7 = AC[7]; AC0 = ACout[0]; AC1 = ACout[1]; AC2 = ACout[2]; AC3 = ACout[3];
  //   AC4 = ACout[4]; AC5 = ACout[5]; AC6 = ACout[6]; AC7 = ACout[7]; MQ0 = MQout[0]; MQ1 = MQout[1]; MQ2 = MQout[2];
  //   MQ3 = MQout[3]; MQ4 = MQout[4]; MQ5 = MQout[5]; MQ6 = MQout[6]; MQ7 = MQout[7]
endmodule
