// Digital circuit multiplicador4bits.dig as structural Verilog
module multiplicador4bits (
  input  B0,
  input  A0,
  input  A1,
  input  B1,
  input  A0_2,
  input  A1_2,
  input  A2,
  input  B2,
  input  A2_2,
  input  A0_3,
  input  A1_3,
  input  A2_3,
  input  A3,
  input  A3_2,
  input  A3_3,
  input  A0_4,
  input  A1_4,
  input  A2_4,
  input  A3_4,
  input  B3,
  output P0,
  output P1,
  output P2,
  output P3,
  output P4,
  output P5,
  output P7,
  output P6
);

  wire and_1_out, and_2_out, and_3_out, and_4_out, and_5_out, and_6_out, and_7_out, and_8_out, and_9_out,
       and_10_out, and_11_out, and_12_out, and_13_out, and_14_out, and_15_out, meio_somador_1_c,
       meio_somador_1_s, meio_somador_2_c, meio_somador_3_c, meio_somador_4_c, somador1bit_2_cout,
       somador1bit_2_s, somador1bit_3_cout, somador1bit_4_cout, somador1bit_4_s, somador1bit_5_cout,
       somador1bit_6_cout, somador1bit_6_s, somador1bit_7_cout, somador1bit_7_s, somador1bit_8_cout,
       somador1bit_8_s;

  and and_1 (and_1_out, A3_4, B3);
  somador1bit somador1bit_1 (.A(somador1bit_3_cout), .B(somador1bit_2_cout), .Cin(and_1_out), .S(P6), .Cout(P7));
  and and_2 (and_2_out, A3_3, B2);
  somador1bit somador1bit_2 (
    .A(somador1bit_4_cout), .B(meio_somador_1_c), .Cin(and_2_out), .S(somador1bit_2_s),
    .Cout(somador1bit_2_cout));
  and and_3 (and_3_out, A2_4, B3);
  somador1bit somador1bit_3 (
    .A(somador1bit_5_cout), .B(and_3_out), .Cin(somador1bit_2_s), .S(P5), .Cout(somador1bit_3_cout));
  and and_4 (and_4_out, A3_2, B1);
  meio_somador meio_somador_1 (.A(somador1bit_6_cout), .B(and_4_out), .S(meio_somador_1_s), .C(meio_somador_1_c));
  and and_5 (and_5_out, A2_3, B2);
  somador1bit somador1bit_4 (
    .A(somador1bit_7_cout), .B(and_5_out), .Cin(meio_somador_1_s), .S(somador1bit_4_s),
    .Cout(somador1bit_4_cout));
  and and_6 (and_6_out, A1_4, B3);
  somador1bit somador1bit_5 (
    .A(meio_somador_2_c), .B(and_6_out), .Cin(somador1bit_4_s), .S(P4), .Cout(somador1bit_5_cout));
  and and_7 (and_7_out, A2_2, B1);
  somador1bit somador1bit_6 (
    .A(somador1bit_8_cout), .B(and_8_out), .Cin(and_7_out), .S(somador1bit_6_s), .Cout(somador1bit_6_cout));
  and and_8 (and_8_out, B0, A3);
  and and_9 (and_9_out, A1_3, B2);
  somador1bit somador1bit_7 (
    .A(meio_somador_3_c), .B(and_9_out), .Cin(somador1bit_6_s), .S(somador1bit_7_s), .Cout(somador1bit_7_cout));
  meio_somador meio_somador_2 (.A(and_10_out), .B(somador1bit_7_s), .S(P3), .C(meio_somador_2_c));
  and and_10 (and_10_out, A0_4, B3);
  and and_11 (and_11_out, A1_2, B1);
  somador1bit somador1bit_8 (
    .A(meio_somador_4_c), .B(and_12_out), .Cin(and_11_out), .S(somador1bit_8_s), .Cout(somador1bit_8_cout));
  and and_12 (and_12_out, B0, A2);
  and and_13 (and_13_out, A0_3, B2);
  meio_somador meio_somador_3 (.A(and_13_out), .B(somador1bit_8_s), .S(P2), .C(meio_somador_3_c));
  and and_14 (and_14_out, A0_2, B1);
  meio_somador meio_somador_4 (.A(and_15_out), .B(and_14_out), .S(P1), .C(meio_somador_4_c));
  and and_15 (and_15_out, B0, A1);
  and and_16 (P0, B0, A0);
endmodule
