// Digital circuit nand8bits.dig as structural Verilog
module nand8bits (
  input  [7:0] A,
  input  [7:0] N,
  output [7:0] ACout
);

  assign ACout = ~(A & N);  // NAnd nand_1, 8 bits wide
endmodule
