// Digital circuit seletor1bit.dig as structural Verilog
module seletor1bit (
  input  A,
  input  B,
  input  C_IN,
  output S,
  output Cout
);

  wire and_1_out, and_2_out, and_3_out;

  xor xor_1 (S, C_IN, A, B);
  and and_1 (and_1_out, C_IN, A);
  and and_2 (and_2_out, C_IN, B);
  and and_3 (and_3_out, A, B);
  or or_1 (Cout, and_1_out, and_2_out, and_3_out);

  // Other names for the same wires on the sheet: Cin = C_IN
endmodule
