// Digital circuit shift.dig as structural Verilog
module shift (
  input  \Direção ,
  input  _0,
  input  _1,
  input  _2,
  input  _3,
  input  _4,
  input  _5,
  input  _6,
  input  _7,
  output _0_2,
  output _1_2,
  output _2_2,
  output _3_2,
  output _4_2,
  output _5_2,
  output _6_2,
  output _7_2
);

  wire and_1_out, and_3_out, and_4_out, and_5_out, and_6_out, and_7_out, and_8_out, and_9_out, and_10_out,
       and_11_out, and_12_out, and_14_out, not_1_out;

  not not_1 (not_1_out, \Direção );
  and and_1 (and_1_out, \Direção , _0);
  and and_2 (_0_2, _1, not_1_out);
  and and_3 (and_3_out, \Direção , _1);
  or or_1 (_1_2, and_4_out, and_1_out);
  and and_4 (and_4_out, _2, not_1_out);
  or or_2 (_2_2, and_6_out, and_3_out);
  and and_5 (and_5_out, \Direção , _2);
  and and_6 (and_6_out, _3, not_1_out);
  or or_3 (_3_2, and_8_out, and_5_out);
  and and_7 (and_7_out, \Direção , _3);
  and and_8 (and_8_out, _4, not_1_out);
  or or_4 (_4_2, and_10_out, and_7_out);
  and and_9 (and_9_out, \Direção , _4);
  and and_10 (and_10_out, _5, not_1_out);
  and and_11 (and_11_out, \Direção , _5);
  or or_5 (_5_2, and_12_out, and_9_out);
  and and_12 (and_12_out, _6, not_1_out);
  or or_6 (_6_2, and_14_out, and_11_out);
  and and_13 (_7_2, \Direção , _6);
  and and_14 (and_14_out, _7, not_1_out);
endmodule
