// Digital circuit somador.dig as structural Verilog
module somador (
  input  [7:0] AC,
  input  [7:0] N,
  output [7:0] S,
  output Overflow
);

  wire somador1bit_1_cout, somador1bit_2_cout, somador1bit_3_cout, somador1bit_4_cout, somador1bit_5_cout,
       somador1bit_6_cout, somador1bit_7_cout;

  somador1bit somador1bit_1 (.A(AC[0]), .B(N[0]), .Cin(1'b0), .S(S[0]), .Cout(somador1bit_1_cout));
  somador1bit somador1bit_2 (.A(AC[1]), .B(N[1]), .Cin(somador1bit_1_cout), .S(S[1]), .Cout(somador1bit_2_cout));
  somador1bit somador1bit_3 (.A(AC[2]), .B(N[2]), .Cin(somador1bit_2_cout), .S(S[2]), .Cout(somador1bit_3_cout));
  somador1bit somador1bit_4 (.A(AC[3]), .B(N[3]), .Cin(somador1bit_3_cout), .S(S[3]), .Cout(somador1bit_4_cout));
  somador1bit somador1bit_5 (.A(AC[4]), .B(N[4]), .Cin(somador1bit_4_cout), .S(S[4]), .Cout(somador1bit_5_cout));
  somador1bit somador1bit_6 (.A(AC[5]), .B(N[5]), .Cin(somador1bit_5_cout), .S(S[5]), .Cout(somador1bit_6_cout));
  somador1bit somador1bit_7 (.A(AC[6]), .B(N[6]), .Cin(somador1bit_6_cout), .S(S[6]), .Cout(somador1bit_7_cout));
  somador1bit somador1bit_8 (.A(AC[7]), .B(N[7]), .Cin(somador1bit_7_cout), .S(S[7]), .Cout(Overflow));

  // Other names for the same wires on the sheet: A0 = AC[0]; A1 = AC[1]; A2 = AC[2]; A3 = AC[3]; A4 = AC[4];
  //   A5 = AC[5]; A6 = AC[6]; A7 = AC[7]; B0 = N[0]; B1 = N[1]; B2 = N[2]; B3 = N[3]; B4 = N[4]; B5 = N[5]; B6 = N[6];
  //   B7 = N[7]
endmodule
