// Digital circuit subtrator.dig as structural Verilog
module subtrator (
  input  [7:0] AC,
  input  [7:0] N,
  output [7:0] S,
  output Overflow
);

  wire B0, B1, B2, B3, B4, B5, B6, B7, somador1bit_1_cout, somador1bit_2_cout, somador1bit_3_cout,
       somador1bit_4_cout, somador1bit_5_cout, somador1bit_6_cout, somador1bit_7_cout;

  not not_1 (B0, N[0]);
  somador1bit somador1bit_1 (.A(AC[0]), .B(B0), .Cin(1'b1), .S(S[0]), .Cout(somador1bit_1_cout));
  somador1bit somador1bit_2 (.A(AC[1]), .B(B1), .Cin(somador1bit_1_cout), .S(S[1]), .Cout(somador1bit_2_cout));
  somador1bit somador1bit_3 (.A(AC[2]), .B(B2), .Cin(somador1bit_2_cout), .S(S[2]), .Cout(somador1bit_3_cout));
  somador1bit somador1bit_4 (.A(AC[3]), .B(B3), .Cin(somador1bit_3_cout), .S(S[3]), .Cout(somador1bit_4_cout));
  somador1bit somador1bit_5 (.A(AC[4]), .B(B4), .Cin(somador1bit_4_cout), .S(S[4]), .Cout(somador1bit_5_cout));
  somador1bit somador1bit_6 (.A(AC[5]), .B(B5), .Cin(somador1bit_5_cout), .S(S[5]), .Cout(somador1bit_6_cout));
  somador1bit somador1bit_7 (.A(AC[6]), .B(B6), .Cin(somador1bit_6_cout), .S(S[6]), .Cout(somador1bit_7_cout));
  somador1bit somador1bit_8 (.A(AC[7]), .B(B7), .Cin(somador1bit_7_cout), .S(S[7]), .Cout(Overflow));
  // Pins of 1 and 8 bits meet at {B7, B6, B5, B4, B3, B2, B1, B0}
  // Pins of 1 and 8 bits meet at N

  // Other names for the same wires on the sheet: A0 = AC[0]; A1 = AC[1]; A2 = AC[2]; A3 = AC[3]; A4 = AC[4];
  //   A5 = AC[5]; A6 = AC[6]; A7 = AC[7]
endmodule
