// Digital circuit subtrator1bit.dig as structural Verilog
module subtrator1bit (
  input  A,
  input  B,
  input  Cin,
  output D,
  output Cout
);

  wire and_1_out, and_2_out, not_1_out, xor_1_out;

  not not_1 (not_1_out, B);
  and and_1 (and_1_out, A, not_1_out);
  xor xor_1 (xor_1_out, A, not_1_out);
  xor xor_2 (D, xor_1_out, Cin);
  and and_2 (and_2_out, xor_1_out, Cin);
  or or_1 (Cout, and_2_out, and_1_out);
endmodule
