// Digital circuit subtrator8bits.dig as structural Verilog
module subtrator8bits (
  input  A0,
  input  B0,
  input  A1,
  input  B1,
  input  A2,
  input  B2,
  input  A3,
  input  B3,
  input  A4,
  input  B4,
  input  A5,
  input  B5,
  input  A6,
  input  B6,
  input  A7,
  input  B7,
  output D0,
  output D1,
  output D2,
  output D3,
  output D4,
  output D5,
  output D6,
  output D7,
  output Cout
);

  wire and_1_out, and_2_out, and_3_out, and_4_out, and_5_out, and_6_out, and_7_out, and_8_out, and_9_out,
       and_10_out, and_11_out, and_12_out, and_13_out, and_14_out, and_15_out, and_16_out, not_1_out,
       not_2_out, not_3_out, not_4_out, not_5_out, not_6_out, not_7_out, not_8_out, or_2_out, or_3_out,
       or_4_out, or_5_out, or_6_out, or_7_out, or_8_out, xor_1_out, xor_3_out, xor_5_out, xor_7_out,
       xor_9_out, xor_11_out, xor_13_out, xor_15_out;

  not not_1 (not_1_out, B7);
  and and_1 (and_1_out, A7, not_1_out);
  xor xor_1 (xor_1_out, A7, not_1_out);
  xor xor_2 (D7, xor_1_out, or_2_out);
  and and_2 (and_2_out, xor_1_out, or_2_out);
  or or_1 (Cout, and_2_out, and_1_out);
  not not_2 (not_2_out, B6);
  and and_3 (and_3_out, A6, not_2_out);
  xor xor_3 (xor_3_out, A6, not_2_out);
  xor xor_4 (D6, xor_3_out, or_3_out);
  and and_4 (and_4_out, xor_3_out, or_3_out);
  or or_2 (or_2_out, and_4_out, and_3_out);
  not not_3 (not_3_out, B5);
  and and_5 (and_5_out, A5, not_3_out);
  xor xor_5 (xor_5_out, A5, not_3_out);
  xor xor_6 (D5, xor_5_out, or_4_out);
  and and_6 (and_6_out, xor_5_out, or_4_out);
  or or_3 (or_3_out, and_6_out, and_5_out);
  not not_4 (not_4_out, B4);
  and and_7 (and_7_out, A4, not_4_out);
  xor xor_7 (xor_7_out, A4, not_4_out);
  xor xor_8 (D4, xor_7_out, or_5_out);
  and and_8 (and_8_out, xor_7_out, or_5_out);
  or or_4 (or_4_out, and_8_out, and_7_out);
  not not_5 (not_5_out, B3);
  and and_9 (and_9_out, A3, not_5_out);
  xor xor_9 (xor_9_out, A3, not_5_out);
  xor xor_10 (D3, xor_9_out, or_6_out);
  and and_10 (and_10_out, xor_9_out, or_6_out);
  or or_5 (or_5_out, and_10_out, and_9_out);
  not not_6 (not_6_out, B2);
  and and_11 (and_11_out, A2, not_6_out);
  xor xor_11 (xor_11_out, A2, not_6_out);
  xor xor_12 (D2, xor_11_out, or_7_out);
  and and_12 (and_12_out, xor_11_out, or_7_out);
  or or_6 (or_6_out, and_12_out, and_11_out);
  not not_7 (not_7_out, B1);
  and and_13 (and_13_out, A1, not_7_out);
  xor xor_13 (xor_13_out, A1, not_7_out);
  xor xor_14 (D1, xor_13_out, or_8_out);
  and and_14 (and_14_out, xor_13_out, or_8_out);
  or or_7 (or_7_out, and_14_out, and_13_out);
  not not_8 (not_8_out, B0);
  and and_15 (and_15_out, A0, not_8_out);
  xor xor_15 (xor_15_out, A0, not_8_out);
  xor xor_16 (D0, xor_15_out, 1'b1);
  and and_16 (and_16_out, xor_15_out, 1'b1);
  or or_8 (or_8_out, and_16_out, and_15_out);
endmodule
