// Digital circuit subtrator_restaurativo1bit.dig as structural Verilog
module subtrator_restaurativo1bit (
  input  A,
  input  B,
  input  Cin,
  input  S,
  output Cout,
  output R
);

  wire tBnot, tSub;

  not not_1 (tBnot, B);
  seletor1bit seletor1bit_1 (.A(tBnot), .B(Cin), .C_IN(A), .S(tSub), .Cout(Cout));
  Multiplexer multiplexer_1 (.sel(S), .in_0(A), .in_1(tSub), .out(R));

  // Other names for the same wires on the sheet: tA = A; tCin = Cin; tCout = Cout
endmodule
