// Digital circuit subtrator_restaurativo8bits.dig as structural Verilog
module subtrator_restaurativo8bits (
  input  [7:0] A,
  input  [7:0] B,
  input  S,
  output [7:0] R,
  output C
);

  wire subtrator_restaurativo1bit_1_cout, subtrator_restaurativo1bit_2_cout,
       subtrator_restaurativo1bit_3_cout, subtrator_restaurativo1bit_4_cout,
       subtrator_restaurativo1bit_5_cout, subtrator_restaurativo1bit_6_cout,
       subtrator_restaurativo1bit_7_cout;

  subtrator_restaurativo1bit subtrator_restaurativo1bit_1 (
    .A(A[0]), .B(B[0]), .Cin(1'b1), .S(S), .Cout(subtrator_restaurativo1bit_1_cout), .R(R[0]));
  subtrator_restaurativo1bit subtrator_restaurativo1bit_2 (
    .A(A[1]), .B(B[1]), .Cin(subtrator_restaurativo1bit_1_cout), .S(S),
    .Cout(subtrator_restaurativo1bit_2_cout), .R(R[1]));
  subtrator_restaurativo1bit subtrator_restaurativo1bit_3 (
    .A(A[2]), .B(B[2]), .Cin(subtrator_restaurativo1bit_2_cout), .S(S),
    .Cout(subtrator_restaurativo1bit_3_cout), .R(R[2]));
  subtrator_restaurativo1bit subtrator_restaurativo1bit_4 (
    .A(A[3]), .B(B[3]), .Cin(subtrator_restaurativo1bit_3_cout), .S(S),
    .Cout(subtrator_restaurativo1bit_4_cout), .R(R[3]));
  subtrator_restaurativo1bit subtrator_restaurativo1bit_5 (
    .A(A[4]), .B(B[4]), .Cin(subtrator_restaurativo1bit_4_cout), .S(S),
    .Cout(subtrator_restaurativo1bit_5_cout), .R(R[4]));
  subtrator_restaurativo1bit subtrator_restaurativo1bit_6 (
    .A(A[5]), .B(B[5]), .Cin(subtrator_restaurativo1bit_5_cout), .S(S),
    .Cout(subtrator_restaurativo1bit_6_cout), .R(R[5]));
  subtrator_restaurativo1bit subtrator_restaurativo1bit_7 (
    .A(A[6]), .B(B[6]), .Cin(subtrator_restaurativo1bit_6_cout), .S(S),
    .Cout(subtrator_restaurativo1bit_7_cout), .R(R[6]));
  subtrator_restaurativo1bit subtrator_restaurativo1bit_8 (
    .A(A[7]), .B(B[7]), .Cin(subtrator_restaurativo1bit_7_cout), .S(S), .Cout(C), .R(R[7]));
endmodule
